// Logisim project control-logic.circ as structural Verilog: 1 circuit, main circuit control_logic
module control_logic (
  input  [31:0] Instruction,
  input  BrEq,
  input  BrLt,
  output PCSel,
  output RegWEn,
  output [2:0] ImmSel,
  output BrUn,
  output ASel,
  output BSel,
  output [3:0] ALUSel,
  output MemWEn,
  output [1:0] WBSel
);

  wire and_1_out, and_2_out, and_3_out, comparator_1_eq, comparator_2_eq, comparator_3_eq, comparator_4_eq,
       comparator_5_eq, comparator_6_eq, comparator_7_eq, comparator_8_eq, not_1_out, not_2_out, or_1_out,
       or_2_out;
  wire [1:0] OPut;
  wire [3:0] adder_1_out, bit_extender_1_out, bit_extender_2_out, bit_extender_3_out, bit_extender_4_out,
       multiplexer_2_out, multiplexer_3_out, multiplexer_4_out;
  wire [7:2] multiplexer_1_out;
  wire [15:0] rom_1_data;
  wire [16:0] BandJals, IandAUIPC, multiplexer_6_out, RandLUI;

  Comparator #(.mode("unsigned"), .width(3)) comparator_1 (
    .a(Instruction[14:12]), .b(3'b101), .eq(comparator_1_eq));  // open: gt, lt
  Comparator #(.mode("unsigned"), .width(7)) comparator_2 (
    .a(Instruction[31:25]), .b(7'b0100000), .eq(comparator_2_eq));  // open: gt, lt
  not not_1 (not_1_out, BrLt);
  ROM #(.addrWidth(6), .dataWidth(16)) rom_1 (.data(rom_1_data));  // open: addr
  Comparator #(.mode("unsigned"), .width(7)) comparator_3 (
    .a(Instruction[31:25]), .b(7'b0000001), .eq(comparator_3_eq));  // open: gt, lt
  and and_1 (and_1_out, comparator_1_eq, comparator_2_eq);
  or or_1 (or_1_out, BrEq, not_1_out);
  Comparator #(.mode("unsigned"), .width(3)) comparator_4 (
    .a(Instruction[14:12]), .b(3'b101), .eq(comparator_4_eq));  // open: gt, lt
  or or_2 (or_2_out, comparator_3_eq, and_1_out);
  and and_2 (and_2_out, comparator_4_eq, Instruction[30]);
  not not_2 (not_2_out, BrEq);
  assign bit_extender_1_out = {{1{1'b1}}, Instruction[14:12]};  // Bit_Extender bit_extender_1
  assign bit_extender_2_out = {{1{1'b0}}, Instruction[14:12]};  // Bit_Extender bit_extender_2
  assign bit_extender_3_out = {{1{1'b1}}, Instruction[14:12]};  // Bit_Extender bit_extender_3
  Comparator #(.mode("unsigned"), .width(3)) comparator_5 (
    .a(Instruction[14:12]), .b(3'b000), .eq(comparator_5_eq));  // open: gt, lt
  Comparator #(.mode("unsigned"), .width(7)) comparator_6 (
    .a(Instruction[31:25]), .b(7'b0100000), .eq(comparator_6_eq));  // open: gt, lt
  Multiplexer #(.select(3)) multiplexer_1 (
    .in0(BrEq), .in1(not_2_out), .in4(BrLt), .in5(or_1_out), .in6(BrLt), .in7(or_1_out),
    .out(multiplexer_1_out[2]), .sel(Instruction[14:12]));  // open: in2, in3
  Comparator #(.mode("unsigned"), .width(3)) comparator_7 (
    .a(3'b111), .b(Instruction[14:12]), .eq(comparator_7_eq));  // open: gt, lt
  Comparator #(.mode("unsigned"), .width(3)) comparator_8 (
    .a(3'b110), .b(Instruction[14:12]), .eq(comparator_8_eq));  // open: gt, lt
  assign bit_extender_4_out = {{1{1'b0}}, Instruction[14:12]};  // Bit_Extender bit_extender_4
  Multiplexer #(.width(4)) multiplexer_2 (
    .in0(bit_extender_4_out), .in1(bit_extender_1_out), .out(multiplexer_2_out), .sel(and_2_out));
  Multiplexer #(.width(4)) multiplexer_3 (
    .in0(bit_extender_2_out), .in1(bit_extender_3_out), .out(multiplexer_3_out), .sel(or_2_out));
  and and_3 (and_3_out, comparator_5_eq, comparator_6_eq);
  or or_3 (multiplexer_1_out[7], comparator_7_eq, comparator_8_eq);
  Multiplexer #(.width(4)) multiplexer_4 (
    .in0(multiplexer_3_out), .in1(adder_1_out), .out(multiplexer_4_out), .sel(and_3_out));
  Adder #(.width(4)) adder_1 (.a(multiplexer_3_out), .b(4'b1100), .out(adder_1_out));  // open: cin, cout
  Multiplexer #(.width(17)) multiplexer_5 (
    .in0({3'b010, multiplexer_2_out, 10'h308}), .in1(17'h8238), .out(IandAUIPC), .sel(Instruction[2]));
  Multiplexer #(.width(17)) multiplexer_6 (
    .in0(17'h1030c), .in1(17'h1024c), .out(multiplexer_6_out), .sel(Instruction[3]));
  Multiplexer #(.width(17)) multiplexer_7 (
    .in0({3'b010, multiplexer_4_out, 10'h108}), .in1(17'hbe38), .out(RandLUI), .sel(Instruction[2]));
  Multiplexer #(.width(17)) multiplexer_8 (
    .in0({9'h2, multiplexer_1_out[7], 4'b0100, multiplexer_1_out[2], 2'b00}), .in1(multiplexer_6_out),
    .out(BandJals), .sel(Instruction[2]));
  Multiplexer #(.select(3), .width(17)) multiplexer_9 (
    .in0(17'h308), .in1(IandAUIPC), .in2(17'h4310), .in3(RandLUI), .in6(BandJals),
    .out({WBSel, MemWEn, ALUSel, BSel, ASel, BrUn, ImmSel, RegWEn, PCSel, OPut}), .sel(Instruction[6:4]));  // open: in4, in5, in7

  // Other names for the same wires on the sheet: OPut[16:2] = {WBSel, MemWEn, ALUSel, BSel, ASel, BrUn, ImmSel, RegWEn, PCSel}

  // Notes on the sheet:
  //   I-Type Arithmetic
  //   R-Type 
  //   B-Type
  //   Load Instructions
  //   Save Instructions
  //   INPUTS to your circuit
  //   Connect ROM Input here ->
  //   ROM FOR CONTROL LOGIC
  //   DON'T CHANGE THE LOCATIONS OF THE INPUTS AND OUTPUTS!
  //   Output = 17 bits. Messed up, these two are inputs, too lazy to fix it(0 BrEq, 1 BrLt,) 2 PCSel, 3 RegWEn, 4,5,6 ImmSel, 7 BrUn, 8 ASel, 9 BSel, 10,11,12 ,13 ALUSEL, 14 MemWEn, 15,16 WBSel
  //   This is only if you choose to do the ROM option
  //   CONNECT
  //   WIRE
  //   TO
  //   USE
  //   ROM
  //   OUTPUT from your circuit
  //   Jal
  //   JalR
  //   Reminder: If using ROM, use combinational logic for PCSel
endmodule
