// Logisim project regfile.circ as structural Verilog: 1 circuit, main circuit regfile
module regfile (
  input  [4:0] ReadIndex1,
  input  [4:0] ReadIndex2,
  input  [4:0] WriteIndex,
  input  [31:0] WriteData,
  input  RegWEn,
  input  clk,
  output [31:0] ra,
  output [31:0] sp,
  output [31:0] t0,
  output [31:0] t1,
  output [31:0] t2,
  output [31:0] s0,
  output [31:0] s1,
  output [31:0] a0,
  output [31:0] ReadData1,
  output [31:0] ReadData2
);

  wire Reg0WE, Reg1WE, Reg2WE, Reg3WE, Reg4WE, Reg5WE, Reg6WE, Reg7WE, Reg8WE, Reg9WE, Reg10WE, Reg11WE,
       Reg12WE, Reg13WE, Reg14WE, Reg15WE, Reg16WE, Reg17WE, Reg18WE, Reg19WE, Reg20WE, Reg21WE, Reg22WE,
       Reg23WE, Reg24WE, Reg25WE, Reg26WE, Reg27WE, Reg28WE, Reg29WE, Reg30WE, Reg31WE;
  wire [31:0] Re28in, Reg0in, Reg0out, Reg1in, Reg2in, Reg3in, Reg3out, Reg4in, Reg4out, Reg5in, Reg6in,
       Reg7in, Reg8in, Reg9in, Reg10in, Reg11in, Reg11out, Reg12in, Reg12out, Reg13in, Reg13out, Reg14in,
       Reg14out, Reg15in, Reg15out, Reg16in, Reg16out, Reg17in, Reg17out, Reg18in, Reg18out, Reg19in,
       Reg19out, Reg20in, Reg20out, Reg21in, Reg21out, Reg22in, Reg22out, Reg23in, Reg23out, Reg24in,
       Reg24out, Reg25in, Reg25out, Reg26in, Reg26out, Reg27in, Reg27out, Reg28in, Reg28out, Reg29in,
       Reg29out, Reg30in, Reg30out, Reg31in, Reg31out;

  Register #(.width(32)) register_1 (.D({32{1'b0}}), .en(1'b0), .clk(clk), .Q(Reg0out));  // open: clr
  Register #(.width(32)) register_2 (.D(Reg4in), .en(Reg4WE), .clk(clk), .Q(Reg4out));  // open: clr
  Register #(.width(32)) register_3 (.D(Reg8in), .en(Reg8WE), .clk(clk), .Q(s0));  // open: clr
  Register #(.width(32)) register_4 (.D(Reg12in), .en(Reg12WE), .clk(clk), .Q(Reg12out));  // open: clr
  Register #(.width(32)) register_5 (.D(Reg16in), .en(Reg16WE), .clk(clk), .Q(Reg16out));  // open: clr
  Register #(.width(32)) register_6 (.D(Reg20in), .en(Reg20WE), .clk(clk), .Q(Reg20out));  // open: clr
  Register #(.width(32)) register_7 (.D(Reg24in), .en(Reg24WE), .clk(clk), .Q(Reg24out));  // open: clr
  Register #(.width(32)) register_8 (.D(Re28in), .en(Reg28WE), .clk(clk), .Q(Reg28out));  // open: clr
  Register #(.width(32)) register_9 (.D(Reg1in), .en(Reg1WE), .clk(clk), .Q(ra));  // open: clr
  Register #(.width(32)) register_10 (.D(Reg5in), .en(Reg5WE), .clk(clk), .Q(t0));  // open: clr
  Register #(.width(32)) register_11 (.D(Reg9in), .en(Reg9WE), .clk(clk), .Q(s1));  // open: clr
  Register #(.width(32)) register_12 (.D(Reg13in), .en(Reg13WE), .clk(clk), .Q(Reg13out));  // open: clr
  Register #(.width(32)) register_13 (.D(Reg17in), .en(Reg17WE), .clk(clk), .Q(Reg17out));  // open: clr
  Register #(.width(32)) register_14 (.D(Reg21in), .en(Reg21WE), .clk(clk), .Q(Reg21out));  // open: clr
  Register #(.width(32)) register_15 (.D(Reg25in), .en(Reg25WE), .clk(clk), .Q(Reg25out));  // open: clr
  Register #(.width(32)) register_16 (.D(Reg29in), .en(Reg29WE), .clk(clk), .Q(Reg29out));  // open: clr
  Multiplexer #(.select(5), .width(32)) multiplexer_1 (
    .in0(Reg0out), .in1(ra), .in2(sp), .in3(Reg3out), .in4(Reg4out), .in5(t0), .in6(t1), .in7(t2), .in8(s0),
    .in9(s1), .in10(a0), .in11(Reg11out), .in12(Reg12out), .in13(Reg13out), .in14(Reg14out), .in15(Reg15out),
    .in16(Reg16out), .in17(Reg17out), .in18(Reg18out), .in19(Reg19out), .in20(Reg20out), .in21(Reg21out),
    .in22(Reg22out), .in23(Reg23out), .in24(Reg24out), .in25(Reg25out), .in26(Reg26out), .in27(Reg27out),
    .in28(Reg28out), .in29(Reg29out), .in30(Reg30out), .in31(Reg31out), .out(ReadData1), .sel(ReadIndex1));
  Register #(.width(32)) register_17 (.D(Reg2in), .en(Reg2WE), .clk(clk), .Q(sp));  // open: clr
  Register #(.width(32)) register_18 (.D(Reg6in), .en(Reg6WE), .clk(clk), .Q(t1));  // open: clr
  Register #(.width(32)) register_19 (.D(Reg10in), .en(Reg10WE), .clk(clk), .Q(a0));  // open: clr
  Register #(.width(32)) register_20 (.D(Reg14in), .en(Reg14WE), .clk(clk), .Q(Reg14out));  // open: clr
  Register #(.width(32)) register_21 (.D(Reg18in), .en(Reg18WE), .clk(clk), .Q(Reg18out));  // open: clr
  Register #(.width(32)) register_22 (.D(Reg22in), .en(Reg22WE), .clk(clk), .Q(Reg22out));  // open: clr
  Register #(.width(32)) register_23 (.D(Reg26in), .en(Reg26WE), .clk(clk), .Q(Reg26out));  // open: clr
  Register #(.width(32)) register_24 (.D(Reg30in), .en(Reg30WE), .clk(clk), .Q(Reg30out));  // open: clr
  Register #(.width(32)) register_25 (.D(Reg3in), .en(Reg3WE), .clk(clk), .Q(Reg3out));  // open: clr
  Register #(.width(32)) register_26 (.D(Reg7in), .en(Reg7WE), .clk(clk), .Q(t2));  // open: clr
  Register #(.width(32)) register_27 (.D(Reg11in), .en(Reg11WE), .clk(clk), .Q(Reg11out));  // open: clr
  Register #(.width(32)) register_28 (.D(Reg15in), .en(Reg15WE), .clk(clk), .Q(Reg15out));  // open: clr
  Register #(.width(32)) register_29 (.D(Reg19in), .en(Reg19WE), .clk(clk), .Q(Reg19out));  // open: clr
  Register #(.width(32)) register_30 (.D(Reg23in), .en(Reg23WE), .clk(clk), .Q(Reg23out));  // open: clr
  Register #(.width(32)) register_31 (.D(Reg27in), .en(Reg27WE), .clk(clk), .Q(Reg27out));  // open: clr
  Register #(.width(32)) register_32 (.D(Reg31in), .en(Reg31WE), .clk(clk), .Q(Reg31out));  // open: clr
  Multiplexer #(.select(5), .width(32)) multiplexer_2 (
    .in0(Reg0out), .in1(ra), .in2(sp), .in3(Reg3out), .in4(Reg4out), .in5(t0), .in6(t1), .in7(t2), .in8(s0),
    .in9(s1), .in10(a0), .in11(Reg11out), .in12(Reg12out), .in13(Reg13out), .in14(Reg14out), .in15(Reg15out),
    .in16(Reg16out), .in17(Reg17out), .in18(Reg18out), .in19(Reg19out), .in20(Reg20out), .in21(Reg21out),
    .in22(Reg22out), .in23(Reg23out), .in24(Reg24out), .in25(Reg25out), .in26(Reg26out), .in27(Reg27out),
    .in28(Reg28out), .in29(Reg29out), .in30(Reg30out), .in31(Reg31out), .out(ReadData2), .sel(ReadIndex2));
  Demultiplexer #(.select(5)) demultiplexer_1 (
    .out0(Reg0WE), .out1(Reg1WE), .out2(Reg2WE), .out3(Reg3WE), .out4(Reg4WE), .out5(Reg5WE), .out6(Reg6WE),
    .out7(Reg7WE), .out8(Reg8WE), .out9(Reg9WE), .out10(Reg10WE), .out11(Reg11WE), .out12(Reg12WE),
    .out13(Reg13WE), .out14(Reg14WE), .out15(Reg15WE), .out16(Reg16WE), .out17(Reg17WE), .out18(Reg18WE),
    .out19(Reg19WE), .out20(Reg20WE), .out21(Reg21WE), .out22(Reg22WE), .out23(Reg23WE), .out24(Reg24WE),
    .out25(Reg25WE), .out26(Reg26WE), .out27(Reg27WE), .out28(Reg28WE), .out29(Reg29WE), .out30(Reg30WE),
    .out31(Reg31WE), .in(RegWEn), .sel(WriteIndex));
  Demultiplexer #(.select(5), .width(32)) demultiplexer_2 (
    .out0(Reg0in), .out1(Reg1in), .out2(Reg2in), .out3(Reg3in), .out4(Reg4in), .out5(Reg5in), .out6(Reg6in),
    .out7(Reg7in), .out8(Reg8in), .out9(Reg9in), .out10(Reg10in), .out11(Reg11in), .out12(Reg12in),
    .out13(Reg13in), .out14(Reg14in), .out15(Reg15in), .out16(Reg16in), .out17(Reg17in), .out18(Reg18in),
    .out19(Reg19in), .out20(Reg20in), .out21(Reg21in), .out22(Reg22in), .out23(Reg23in), .out24(Reg24in),
    .out25(Reg25in), .out26(Reg26in), .out27(Reg27in), .out28(Reg28in), .out29(Reg29in), .out30(Reg30in),
    .out31(Reg31in), .in(WriteData), .sel(WriteIndex));

  // Other names for the same wires on the sheet: Reg1out[31:0] = ra; Reg2out[31:0] = sp; Reg5out[31:0] = t0;
  //   Reg6out[31:0] = t1; Reg7out[31:0] = t2; Reg8out[31:0] = s0; Reg9out[31:0] = s1; Reg10out[31:0] = a0

  // Notes on the sheet:
  //   INPUTS to your circuit
  //   DON'T CHANGE THE LOCATIONS OF THE INPUTS AND OUTPUTS!
  //   These are DEBUG/TEST outputs from your circuit.
  //   OUTPUTS from your circuit
endmodule
