// Logisim project cpu.circ as structural Verilog: 1 circuit, main circuit cpu
module cpu (
  input  clk,
  input  [31:0] Instruction,
  input  [31:0] MemReadData,
  output [31:0] MemAddress,
  output [31:0] ProgramCounter,
  output [31:0] ra,
  output [31:0] sp,
  output [31:0] t0,
  output [31:0] t1,
  output [31:0] t2,
  output [31:0] s0,
  output [31:0] s1,
  output [31:0] a0,
  output [3:0] MemWriteMask,
  output [31:0] MemWriteData
);

  wire and_1_out, Asel, BrEq, BrLt, BrUn, Bsel, comparator_1_eq, comparator_2_eq, comparator_3_eq,
       comparator_4_eq, Flush, MemWEn, multiplexer_1_out, multiplexer_4_out, multiplexer_7_out, or_1_out,
       PCSel, RegWEn;
  wire [1:0] WBSel;
  wire [2:0] ImmSel;
  wire [3:0] ALUsel;
  wire [31:0] adder_1_out, imm_gen_1_immediate, multiplexer_2_out, multiplexer_5_out, multiplexer_6_out,
       partial_load_1_datatoreg, PipInstruction, regfile_1_readdata1, regfile_1_readdata2, register_1_q,
       register_2_q, register_3_q, WBOut;

  Multiplexer multiplexer_1 (.in0(PCSel), .in1(1'b0), .out(multiplexer_1_out), .sel(Flush));
  Multiplexer #(.width(32)) multiplexer_2 (
    .in0(adder_1_out), .in1(MemAddress), .out(multiplexer_2_out), .sel(multiplexer_1_out));
  Register #(.width(32)) PC (.D(multiplexer_2_out), .clk(clk), .Q(ProgramCounter));  // open: en, clr
  Register #(.width(32)) register_1 (.D(ProgramCounter), .clk(clk), .Q(register_1_q));  // open: en, clr
  Register #(.width(32)) register_2 (.D(Instruction), .clk(clk), .Q(register_2_q));  // open: en, clr
  Register #(.width(32)) register_3 (.D(adder_1_out), .clk(clk), .Q(register_3_q));  // open: en, clr
  Adder #(.width(32)) adder_1 (.a(ProgramCounter), .b(32'h4), .out(adder_1_out));  // open: cin, cout
  Multiplexer #(.width(32)) multiplexer_3 (.in0(register_2_q), .in1(32'h13), .out(PipInstruction), .sel(Flush));
  Multiplexer multiplexer_4 (.in0(RegWEn), .in1(1'b0), .out(multiplexer_4_out), .sel(Flush));
  regfile regfile_1 (
    .ReadIndex1(PipInstruction[19:15]), .ReadIndex2(PipInstruction[24:20]),
    .WriteIndex(PipInstruction[11:7]), .WriteData(WBOut), .RegWEn(multiplexer_4_out), .clk(clk), .ra(ra),
    .sp(sp), .t0(t0), .t1(t1), .t2(t2), .s0(s0), .s1(s1), .a0(a0), .ReadData1(regfile_1_readdata1),
    .ReadData2(regfile_1_readdata2));
  imm_gen imm_gen_1 (.Instruction(PipInstruction), .ImmSel(ImmSel), .Immediate(imm_gen_1_immediate));
  Multiplexer #(.width(32)) multiplexer_5 (
    .in0(regfile_1_readdata2), .in1(imm_gen_1_immediate), .out(multiplexer_5_out), .sel(Bsel));
  Multiplexer #(.width(32)) multiplexer_6 (
    .in0(register_1_q), .in1(regfile_1_readdata1), .out(multiplexer_6_out), .sel(Asel));
  branch_comp branch_comp_1 (
    .BrData1(regfile_1_readdata1), .BrData2(regfile_1_readdata2), .BrUn(BrUn), .BrEq(BrEq), .BrLt(BrLt));
  control_logic control_logic_1 (
    .PCSel(PCSel), .RegWEn(RegWEn), .ImmSel(ImmSel), .BrUn(BrUn), .ASel(Asel), .BSel(Bsel), .ALUSel(ALUsel),
    .MemWEn(MemWEn), .WBSel(WBSel), .Instruction(PipInstruction), .BrEq(BrEq), .BrLt(BrLt));
  alu alu_1 (.ALUResult(MemAddress), .A(multiplexer_6_out), .B(multiplexer_5_out), .ALUSel(ALUsel));
  Comparator #(.mode("unsigned"), .width(7)) comparator_1 (
    .a(PipInstruction[6:0]), .b(7'b1101111), .eq(comparator_1_eq));  // open: gt, lt
  Comparator #(.mode("unsigned"), .width(7)) comparator_2 (
    .a(PipInstruction[6:0]), .b(7'b1100111), .eq(comparator_2_eq));  // open: gt, lt
  Comparator #(.mode("unsigned"), .width(7)) comparator_3 (
    .a(PipInstruction[6:0]), .b(7'b1100011), .eq(comparator_3_eq));  // open: gt, lt
  Comparator #(.mode("unsigned"), .width(1)) comparator_4 (.a(PCSel), .b(1'b1), .eq(comparator_4_eq));  // open: gt, lt
  and and_1 (and_1_out, comparator_3_eq, comparator_4_eq);
  Multiplexer multiplexer_7 (.in0(MemWEn), .in1(1'b0), .out(multiplexer_7_out), .sel(Flush));
  or or_1 (or_1_out, comparator_1_eq, comparator_2_eq, and_1_out);
  Register #(.width(1)) register_4 (.D(or_1_out), .clk(clk), .Q(Flush));  // open: en, clr
  partial_load partial_load_1 (
    .Instruction(PipInstruction), .MemAddress(MemAddress), .DataFromMem(MemReadData),
    .DataToReg(partial_load_1_datatoreg));
  partial_store partial_store_1 (
    .Instruction(PipInstruction), .MemAddress(MemAddress), .DataFromReg(regfile_1_readdata2),
    .MemWEn(multiplexer_7_out), .MemWriteMask(MemWriteMask), .DataToMem(MemWriteData));
  Multiplexer #(.select(2), .width(32)) multiplexer_8 (
    .in0(partial_load_1_datatoreg), .in1(MemAddress), .in2(register_3_q), .out(WBOut), .sel(WBSel));  // open: in3

  // Notes on the sheet:
  //   To IMEM
  //   IMEM (do **NOT** move this)
  //   From IMEM
  //   Inputs/Outputs for testing. Do **NOT** move these.
  //   To DMEM
  //   DMEM (do **NOT** move this)
  //   From DMEM
endmodule
