// Logisim project partial-store.circ as structural Verilog: 1 circuit, main circuit partial_store
module partial_store (
  input  [31:0] Instruction,
  input  [31:0] MemAddress,
  input  [31:0] DataFromReg,
  input  MemWEn,
  output [3:0] MemWriteMask,
  output [31:0] DataToMem
);

  wire [35:0] answer, multiplexer_2_out, multiplexer_3_out;

  Multiplexer #(.width(36)) multiplexer_1 (
    .in0({36{1'b0}}), .in1(answer), .out({MemWriteMask, DataToMem}), .sel(MemWEn));
  Multiplexer #(.select(2), .width(36)) multiplexer_2 (
    .in0({28'h1000000, DataFromReg[7:0]}), .in1({20'h20000, DataFromReg[7:0], {8{1'b0}}}),
    .in2({12'h400, DataFromReg[7:0], {16{1'b0}}}), .in3({4'b1000, DataFromReg[7:0], {24{1'b0}}}),
    .out(multiplexer_2_out), .sel(MemAddress[1:0]));
  Multiplexer #(.select(2), .width(36)) multiplexer_3 (
    .in0({20'h30000, DataFromReg[15:0]}), .in1({36{1'b0}}), .in2({4'b1100, DataFromReg[15:0], {16{1'b0}}}),
    .in3({36{1'b0}}), .out(multiplexer_3_out), .sel(MemAddress[1:0]));
  Multiplexer #(.select(3), .width(36)) multiplexer_4 (
    .in0(multiplexer_2_out), .in1(multiplexer_3_out), .in2({4'b1111, DataFromReg}), .in3({36{1'b0}}),
    .in4({36{1'b0}}), .in5({36{1'b0}}), .in6({36{1'b0}}), .in7({36{1'b0}}), .out(answer),
    .sel(Instruction[14:12]));

  // Other names for the same wires on the sheet: Func3[2:0] = Instruction[14:12]; Bot2[1:0] = MemAddress[1:0]

  // Notes on the sheet:
  //   INPUTS to your circuit
  //   DON'T CHANGE THE LOCATIONS OF THE INPUTS AND OUTPUTS!
  //   OUTPUT from your circuit
endmodule
